// Digital circuit DATA-MEMORY.dig as structural Verilog
module DATA_MEMORY (
  input  load,
  input  [31:0] rwaddr,
  input  clk,
  input  [31:0] wdata,
  input  dmwen,
  input  [2:0] f3,
  output [31:0] out,
  output [31:0] out_read
);

  wire comparator_2_eq, comparator_3_eq, OR0, OR1, OR2, str0, str1, str2, str3;

  Comparator #(.Bits(3)) comparator_1 (.a(3'b010), .b(f3), .eq(OR2));  // open: gt, lt
  Comparator #(.Bits(3)) comparator_2 (.a(3'b001), .b(f3), .eq(comparator_2_eq));  // open: gt, lt
  Comparator #(.Bits(3)) comparator_3 (.a(3'b000), .b(f3), .eq(comparator_3_eq));  // open: gt, lt
  and and_1 (str0, dmwen, OR0);
  or or_1 (OR0, OR2, comparator_2_eq, comparator_3_eq);
  and and_2 (str1, dmwen, OR1);
  or or_2 (OR1, OR2, comparator_2_eq);
  BlockRAMDualPort #(.AddrBits(24), .Bits(8)) blockramdualport_1 (
    .A(rwaddr[23:0]), .Din(wdata[7:0]), .str(str0), .C(clk), .D(out[7:0]));
  and and_3 (str2, dmwen, OR2);
  BlockRAMDualPort #(.AddrBits(24), .Bits(8)) blockramdualport_2 (
    .A(rwaddr[23:0]), .Din(wdata[15:8]), .str(str1), .C(clk), .D(out[15:8]));
  and and_4 (str3, dmwen, OR2);
  BlockRAMDualPort #(.AddrBits(24), .Bits(8)) blockramdualport_3 (
    .A(rwaddr[23:0]), .Din(wdata[23:16]), .str(str2), .C(clk), .D(out[23:16]));
  BlockRAMDualPort #(.AddrBits(24), .Bits(8)) blockramdualport_4 (
    .A(rwaddr[23:0]), .Din(wdata[31:24]), .str(str3), .C(clk), .D(out[31:24]));
  Multiplexer #(.Bits(8)) multiplexer_1 (.sel(OR0), .in_0({8{1'b0}}), .in_1(out[7:0]), .out(out_read[7:0]));
  Multiplexer #(.Bits(8)) multiplexer_2 (.sel(OR1), .in_0({8{1'b0}}), .in_1(out[15:8]), .out(out_read[15:8]));
  Multiplexer #(.Bits(8)) multiplexer_3 (.sel(OR2), .in_0({8{1'b0}}), .in_1(out[23:16]), .out(out_read[23:16]));
  Multiplexer #(.Bits(8)) multiplexer_4 (.sel(OR2), .in_0({8{1'b0}}), .in_1(out[31:24]), .out(out_read[31:24]));

  // Other names for the same wires on the sheet: D0[7:0] = out[7:0]; D1[7:0] = out[15:8]; D2[7:0] = out[23:16];
  //   D3[7:0] = out[31:24]; OR3 = OR2; A[23:0] = rwaddr[23:0]; Din0[7:0] = wdata[7:0]; Din1[7:0] = wdata[15:8];
  //   Din2[7:0] = wdata[23:16]; Din3[7:0] = wdata[31:24]
endmodule
