// Digital circuit alu.dig as structural Verilog
module alu (
  input  [31:0] op_1,
  input  [31:0] op_2,
  input  [2:0] f3,
  input  [6:0] f7,
  output [31:0] out
);

  wire f71, slt_lt, sltu_lt;
  wire [31:0] add, addsub, \and , \or , sll, slt, sltu, sra, srasrl, srl, sub, \xor ;

  Add #(.Bits(32)) add_1 (.a(op_1), .b(op_2), .c_i(1'b0), .s(add));  // open: c_o
  Sub #(.Bits(32)) sub_1 (.a(op_1), .b(op_2), .c_i(1'b0), .s(sub));  // open: c_o
  assign \xor  = op_1 ^ op_2;  // XOr xor_1, 32 bits wide
  assign \or  = op_1 | op_2;  // Or or_1, 32 bits wide
  assign \and  = op_1 & op_2;  // And and_1, 32 bits wide
  BarrelShifter #(.Bits(32)) u_sll (.in(op_1), .shift(op_2[5:0]), .out(sll));
  BarrelShifter #(.Bits(32), .direction("right")) u_srl (.in(op_1), .shift(op_2[5:0]), .out(srl));
  BarrelShifter #(.barrelShifterMode("arithmetic"), .Bits(32)) u_sra (.in(op_1), .shift(op_2[5:0]), .out(sra));
  Comparator #(.Signed("true"), .Bits(32)) u_slt (.a(op_1), .b(op_2), .lt(slt_lt));  // open: gt, eq
  Comparator #(.Bits(32)) u_sltu (.a(op_1), .b(op_2), .lt(sltu_lt));  // open: gt, eq
  BitExtender #(.inputBits(1), .outputBits(32)) bitextender_1 (.in(slt_lt), .out(slt));
  BitExtender #(.inputBits(1), .outputBits(32)) bitextender_2 (.in(sltu_lt), .out(sltu));
  Multiplexer #(.Bits(32)) multiplexer_1 (.sel(f71), .in_0(add), .in_1(sub), .out(addsub));
  Multiplexer #(.Bits(32)) multiplexer_2 (.sel(f71), .in_0(sra), .in_1(srl), .out(srasrl));
  Comparator #(.Bits(7)) comparator_1 (.a(f7), .b(7'b0100000), .eq(f71));  // open: gt, lt
  Multiplexer #(.Selector_Bits(3), .Bits(32)) multiplexer_3 (
    .sel(f3), .in_0(addsub), .in_1(sll), .in_2(slt), .in_3(sltu), .in_4(\xor ), .in_5(srasrl), .in_6(\or ),
    .in_7(\and ), .out(out));
  // Probe bin on out
  // Probe dec on out
  // Probe hex on out
endmodule
