// Digital circuit branch.dig as structural Verilog
module branch (
  input  [31:0] rs1data,
  input  [31:0] rs2data,
  input  brinst,
  input  [2:0] \type ,
  input  unbrinst,
  output pc_jump,
  output rs1_pc,
  output eq,
  output lt,
  output ge,
  output ltu,
  output geu
);

  wire and_1_out, and_2_out, and_3_out, and_4_out, and_5_out, and_6_out, bltu_2_eq, bltu_eq, comparator_3_eq,
       comparator_4_eq, comparator_5_eq, comparator_6_eq, equ, gt, gtu, multiplexer_1_out, multiplexer_2_out,
       multiplexer_3_out, multiplexer_4_out, multiplexer_5_out, multiplexer_6_out, ne;

  or or_1 (ge, gt, eq);
  or or_2 (geu, gtu, equ);
  Comparator #(.Signed("true"), .Bits(32)) comparator_1 (.a(rs1data), .b(rs2data), .gt(gtu), .eq(equ), .lt(ltu));
  Comparator #(.Bits(32)) comparator_2 (.a(rs1data), .b(rs2data), .gt(gt), .eq(eq), .lt(lt));
  not not_1 (ne, eq);
  Comparator #(.Bits(3)) bltu (.a(3'b111), .b(\type ), .eq(bltu_eq));  // open: gt, lt
  and and_1 (and_1_out, geu, bltu_eq);
  Comparator #(.Bits(3)) bltu_2 (.a(3'b110), .b(\type ), .eq(bltu_2_eq));  // open: gt, lt
  and and_2 (and_2_out, ltu, bltu_2_eq);
  Comparator #(.Bits(3)) comparator_3 (.a(3'b101), .b(\type ), .eq(comparator_3_eq));  // open: gt, lt
  Multiplexer multiplexer_1 (.sel(and_1_out), .in_0(1'b0), .in_1(1'b1), .out(multiplexer_1_out));
  and and_3 (and_3_out, ge, comparator_3_eq);
  Comparator #(.Bits(3)) comparator_4 (.a(3'b100), .b(\type ), .eq(comparator_4_eq));  // open: gt, lt
  Multiplexer multiplexer_2 (.sel(and_2_out), .in_0(multiplexer_1_out), .in_1(1'b1), .out(multiplexer_2_out));
  and and_4 (and_4_out, lt, comparator_4_eq);
  Comparator #(.Bits(3)) comparator_5 (.a(3'b001), .b(\type ), .eq(comparator_5_eq));  // open: gt, lt
  Multiplexer multiplexer_3 (.sel(and_3_out), .in_0(multiplexer_2_out), .in_1(1'b1), .out(multiplexer_3_out));
  and and_5 (and_5_out, ne, comparator_5_eq);
  Comparator #(.Bits(3)) comparator_6 (.a(3'b000), .b(\type ), .eq(comparator_6_eq));  // open: gt, lt
  Multiplexer multiplexer_4 (.sel(and_4_out), .in_0(multiplexer_3_out), .in_1(1'b1), .out(multiplexer_4_out));
  and and_6 (and_6_out, eq, comparator_6_eq);
  Multiplexer multiplexer_5 (.sel(and_5_out), .in_0(multiplexer_4_out), .in_1(1'b1), .out(multiplexer_5_out));
  Multiplexer multiplexer_6 (.sel(and_6_out), .in_0(multiplexer_5_out), .in_1(1'b1), .out(multiplexer_6_out));
  and and_7 (rs1_pc, brinst, multiplexer_6_out);
  or or_3 (pc_jump, unbrinst, rs1_pc);
endmodule
