// Digital circuit circuito-completo.dig as structural Verilog
module circuito_completo (
  input  [31:0] reset,
  input  [31:0] in_2
);

  wire brinst, clk, control_1_p2, deq, dge, dgeu, dlt, dltu, dmwen, jal_jalr, load, opcode, pc_jump, rfwren,
       rs1_pc, sraisub, store;
  wire [1:0] wbsel;
  wire [2:0] f3;
  wire [4:0] instdecoder_1_rd, instdecoder_1_rs1, instdecoder_1_rs2;
  wire [6:0] f7;
  wire [31:0] add_1_s, aluout, data_memory_1_out, multiplexer_1_out, multiplexer_2_out, multiplexer_3_out,
       multiplexer_4_out, notconnected_1_out, pc, rd1, rd2, unitimm_1_imm;

  Multiplexer #(.Bits(32)) multiplexer_1 (.sel(pc_jump), .in_0(add_1_s), .in_1(aluout), .out(multiplexer_1_out));
  Add #(.Bits(32)) add_1 (.a(pc), .b(32'h4), .c_i(1'b0), .s(add_1_s));  // open: c_o
  pc pc_1 (.\input (multiplexer_1_out), .wen(1'b1), .reset(reset), .clk(clk), .\output (pc));
  instdecoder instdecoder_1 (
    .Inst(in_2), .Rd(instdecoder_1_rd), .Rs1(instdecoder_1_rs1), .Rs2(instdecoder_1_rs2), .Funct3(f3),
    .Funct7(f7));  // open: Opcode
  // Probe on pc
  // Probe on rd1
  // Probe on rd2
  // Probe on wbsel
  // Probe on aluout
  unitimm unitimm_1 (.Inst(in_2), .Imm(unitimm_1_imm));
  // control control_1: pin names not known; wires that end beside it: in_2, control_1_p2, rfwren, dmwen, opcode, f3, sraisub, brinst, jal_jalr, wbsel, load, store
  register_file register_file_1 (
    .enable(rfwren), .rdAdrs(instdecoder_1_rd), .rdData(multiplexer_4_out), .rs1Adrs(instdecoder_1_rs1),
    .rs2Adrs(instdecoder_1_rs2), .clock(clk), .rs1Data(rd1), .rs2Data(rd2));
  Multiplexer #(.Bits(32)) multiplexer_2 (
    .sel(control_1_p2), .in_0(rd2), .in_1(unitimm_1_imm), .out(multiplexer_2_out));
  branch branch_1 (
    .rs1data(rd1), .rs2data(rd2), .brinst(brinst), .\type (f3), .unbrinst(jal_jalr), .pc_jump(pc_jump),
    .rs1_pc(rs1_pc), .eq(deq), .lt(dlt), .ge(dge), .ltu(dltu), .geu(dgeu));
  Multiplexer #(.Bits(32)) multiplexer_3 (.sel(rs1_pc), .in_0(rd1), .in_1(pc), .out(multiplexer_3_out));
  alu alu_1 (.op_1(multiplexer_3_out), .op_2(multiplexer_2_out), .f3(f3), .f7(f7), .out(aluout));
  Button button_1 (.out(clk));
  DATA_MEMORY data_memory_1 (
    .rwaddr(aluout), .clk(clk), .wdata(rd2), .dmwen(dmwen), .f3(f3), .out(data_memory_1_out));  // open: load, out_read
  Multiplexer #(.Selector_Bits(2), .Bits(32)) multiplexer_4 (
    .sel(wbsel), .in_0(aluout), .in_1(data_memory_1_out), .in_2(add_1_s), .in_3(notconnected_1_out),
    .out(multiplexer_4_out));
  // NotConnected on notconnected_1_out
  // Pins of 1 and 32 bits meet at reset

  // Other names for the same wires on the sheet: inst[31:0] = in_2
endmodule
