// Digital circuit immsel.dig as structural Verilog
module immsel (
  input  [6:0] Opcode,
  input  [2:0] funct3,
  output [2:0] immsel
);

  wire and_1_out, auipc_eq, B_eq, comparator_1_eq, comparator_2_eq, J_eq, lui_eq, or_1_out, S_eq,
       srai_slli_srli_eq;
  wire [2:0] multiplexer_1_out, multiplexer_2_out, multiplexer_3_out, multiplexer_4_out, multiplexer_5_out;

  Comparator #(.Bits(7)) S (.a(Opcode), .b(7'b0100011), .eq(S_eq));  // open: gt, lt
  Multiplexer #(.Bits(3)) multiplexer_1 (.sel(S_eq), .in_0(3'b000), .in_1(3'b001), .out(multiplexer_1_out));
  Comparator #(.Bits(7)) B (.a(Opcode), .b(7'b1100011), .eq(B_eq));  // open: gt, lt
  Multiplexer #(.Bits(3)) multiplexer_2 (.sel(B_eq), .in_0(multiplexer_1_out), .in_1(3'b010), .out(multiplexer_2_out));
  Comparator #(.Bits(7)) lui (.a(Opcode), .b(7'b0110111), .eq(lui_eq));  // open: gt, lt
  Multiplexer #(.Bits(3)) multiplexer_3 (
    .sel(lui_eq), .in_0(multiplexer_2_out), .in_1(3'b011), .out(multiplexer_3_out));
  Comparator #(.Bits(7)) auipc (.a(Opcode), .b(7'b0010111), .eq(auipc_eq));  // open: gt, lt
  Multiplexer #(.Bits(3)) multiplexer_4 (
    .sel(auipc_eq), .in_0(multiplexer_3_out), .in_1(3'b011), .out(multiplexer_4_out));
  Comparator #(.Bits(7)) J (.a(Opcode), .b(7'b1101111), .eq(J_eq));  // open: gt, lt
  Multiplexer #(.Bits(3)) multiplexer_5 (.sel(J_eq), .in_0(multiplexer_4_out), .in_1(3'b100), .out(multiplexer_5_out));
  Comparator #(.Bits(3)) comparator_1 (.a(funct3), .b(3'b001), .eq(comparator_1_eq));  // open: gt, lt
  Comparator #(.Bits(3)) comparator_2 (.a(funct3), .b(3'b101), .eq(comparator_2_eq));  // open: gt, lt
  Comparator #(.Bits(7)) srai_slli_srli (.a(Opcode), .b(7'b0010011), .eq(srai_slli_srli_eq));  // open: gt, lt
  or or_1 (or_1_out, comparator_1_eq, comparator_2_eq);
  Multiplexer #(.Bits(3)) multiplexer_6 (.sel(and_1_out), .in_0(multiplexer_5_out), .in_1(3'b101), .out(immsel));
  and and_1 (and_1_out, srai_slli_srli_eq, or_1_out);
endmodule
