// Digital circuit pc.dig as structural Verilog
module pc (
  input  [31:0] \input ,
  input  wen,
  input  [31:0] reset,
  input  clk,
  output [31:0] \output 
);

  wire [31:0] multiplexer_1_out;

  Multiplexer #(.Bits(32)) multiplexer_1 (.sel(reset[0]), .in_0(\input ), .in_1({32{1'b0}}), .out(multiplexer_1_out));
  Register #(.Bits(32)) register_1 (.D(multiplexer_1_out), .C(clk), .en(wen), .Q(\output ));
  // Pins of 1 and 32 bits meet at reset
endmodule
