// Digital circuit register.dig as structural Verilog
module register (
  input  [31:0] rdData,
  input  [23:0] rdAdrs,
  input  [23:0] rs1Adrs,
  input  [23:0] rs2Adrs,
  input  CLK,
  input  wrenable,
  output [31:0] rs1data,
  output [31:0] rs2data
);

  wire comparator_1_eq, multiplexer_1_out;

  Comparator #(.Bits(5)) comparator_1 (.a({5{1'b0}}), .b(rdAdrs[4:0]), .eq(comparator_1_eq));  // open: gt, lt
  Multiplexer multiplexer_1 (.sel(comparator_1_eq), .in_0(wrenable), .in_1(1'b0), .out(multiplexer_1_out));
  RegisterFile #(.AddrBits(24), .Bits(32)) registerfile_1 (
    .Din(rdData), .we(multiplexer_1_out), .Rw(rdAdrs), .C(CLK), .Ra(rs1Adrs), .Rb(rs2Adrs), .Da(rs1data),
    .Db(rs2data));
  // Pins of 5 and 24 bits meet at rdAdrs
  // Pins of 5 and 24 bits meet at rs1Adrs
  // Pins of 5 and 24 bits meet at rs2Adrs

  // Other names for the same wires on the sheet: clock = CLK
endmodule
