// Digital circuit unitimm.dig as structural Verilog
module unitimm (
  input  [31:0] Inst,
  output [31:0] Imm
);

  wire [2:0] immsel_1_immsel;
  wire [11:0] Imm_U;
  wire [31:0] notconnected_1_out, notconnected_2_out;
  wire [31:5] shamt_I;
  wire [31:12] Imm_I, Imm_S;
  wire [31:13] Imm_B;
  wire [31:21] Imm_J;
  wire [31:27] bitextender_6_out;

  BitExtender #(.inputBits(1), .outputBits(12)) bitextender_1 (.in(1'b0), .out(Imm_U));
  BitExtender #(.inputBits(1), .outputBits(11)) bitextender_2 (.in(Inst[31]), .out(Imm_J));
  BitExtender #(.inputBits(1), .outputBits(20)) bitextender_3 (.in(Inst[31]), .out(Imm_I));
  BitExtender #(.inputBits(1), .outputBits(20)) bitextender_4 (.in(Inst[31]), .out(Imm_S));
  BitExtender #(.inputBits(1), .outputBits(19)) bitextender_5 (.in(Inst[31]), .out(Imm_B));
  BitExtender #(.inputBits(1), .outputBits(32)) bitextender_6 (.in(1'b0), .out({bitextender_6_out, shamt_I}));
  Multiplexer #(.Selector_Bits(3), .Bits(32)) multiplexer_1 (
    .sel(immsel_1_immsel), .in_0({Imm_I, Inst[31:20]}), .in_1({Imm_S, Inst[31:25], Inst[11:7]}),
    .in_2({Imm_B, Inst[31], Inst[7], Inst[30:25], Inst[11:8], 1'b0}), .in_3({Inst[31:12], Imm_U}),
    .in_4({Imm_J, Inst[31], Inst[19:12], Inst[20], Inst[30:21], 1'b0}), .in_5({shamt_I, Inst[24:20]}),
    .in_6(notconnected_1_out), .in_7(notconnected_2_out), .out(Imm));
  // NotConnected on notconnected_1_out
  // NotConnected on notconnected_2_out
  immsel immsel_1 (.Opcode(Inst[6:0]), .funct3(Inst[14:12]), .immsel(immsel_1_immsel));

  // Other names for the same wires on the sheet: Opcode[6:0] = Inst[6:0];
  //   Imm_B[12:1] = {Inst[31], Inst[7], Inst[30:25], Inst[11:8]}; Imm_S[11:0] = {Inst[31:25], Inst[11:7]};
  //   funct3[2:0] = Inst[14:12]; Imm_J[20:1] = {Inst[31], Inst[19:12], Inst[20], Inst[30:21]};
  //   Imm_U[31:12] = Inst[31:12]; Imm_I[11:0] = Inst[31:20]; shamt_I[4:0] = Inst[24:20]
endmodule
